// Logisim project FlagUnit.circ as structural Verilog: 4 circuits, main circuit overflow
// OverflowCalc
module overflow (
  input  [11:0] Rounded_exponent,
  input  Add_sub,
  output FinalOverflow
);

  wire n7408_1__3__1y, n7408_1__6__2y, n7408_1__8__3y, n7408_1__11__4y, n7408_2__3__1y, n7408_2__6__2y,
       n7408_2__8__3y, n7408_2__11__4y, n7408_3__3__1y, n7408_3__6__2y, Overflow;

  Multiplexer multiplexer_1 (.in0(Overflow), .in1(1'b0), .out(FinalOverflow), .sel(Add_sub), .en(1'b1));
  _7408 u_7408_1 (
    ._1__1A(Rounded_exponent[0]), ._2__1B(Rounded_exponent[1]), ._3__1Y(n7408_1__3__1y),
    ._4__2A(n7408_1__3__1y), ._5__2B(Rounded_exponent[2]), ._6__2Y(n7408_1__6__2y), ._7__GND(1'b0),
    ._14__Vcc(1'b1), ._13__4B(n7408_1__6__2y), ._12__4A(Rounded_exponent[3]), ._11__4Y(n7408_1__11__4y),
    ._10__3B(n7408_1__11__4y), ._9__3A(Rounded_exponent[4]), ._8__3Y(n7408_1__8__3y));
  _7408 u_7408_2 (
    ._1__1A(n7408_1__8__3y), ._2__1B(Rounded_exponent[5]), ._3__1Y(n7408_2__3__1y), ._4__2A(n7408_2__3__1y),
    ._5__2B(Rounded_exponent[6]), ._6__2Y(n7408_2__6__2y), ._7__GND(1'b0), ._14__Vcc(1'b1),
    ._13__4B(n7408_2__6__2y), ._12__4A(Rounded_exponent[7]), ._11__4Y(n7408_2__11__4y),
    ._10__3B(n7408_2__11__4y), ._9__3A(Rounded_exponent[8]), ._8__3Y(n7408_2__8__3y));
  _7408 u_7408_3 (
    ._1__1A(n7408_2__8__3y), ._2__1B(Rounded_exponent[9]), ._3__1Y(n7408_3__3__1y), ._4__2A(n7408_3__3__1y),
    ._5__2B(Rounded_exponent[10]), ._6__2Y(n7408_3__6__2y), ._7__GND(1'b0), ._14__Vcc(1'b1));  // open: _13__4B, _12__4A, _11__4Y, _10__3B, _9__3A, _8__3Y
  _7432 u_7432_1 (
    ._1__1A(n7408_3__6__2y), ._2__1B(Rounded_exponent[11]), ._3__1Y(Overflow), ._7__GND(1'b0), ._14__Vcc(1'b1));  // open: _4__2A, _5__2B, _6__2Y, _13__4B, _12__4A, _11__4Y, _10__3B, _9__3A, _8__3Y
endmodule

// UnderflowCalc
module underflow (
  input  [11:0] Rounded_exponent,
  input  LS_Norm_borrow,
  input  Add_sub,
  output FinalUnderflow
);

  wire n7404_1__2__1y, n7432_1__3__1y, n7432_1__6__2y, n7432_1__8__3y, n7432_1__11__4y, n7432_2__3__1y,
       n7432_2__6__2y, n7432_2__8__3y, n7432_2__11__4y, n7432_3__3__1y, n7432_3__6__2y, n7432_3__11__4y,
       Underflow;

  Multiplexer multiplexer_1 (.in0(1'b0), .in1(Underflow), .out(FinalUnderflow), .sel(Add_sub), .en(1'b1));
  _7432 u_7432_1 (
    ._1__1A(Rounded_exponent[0]), ._2__1B(Rounded_exponent[1]), ._3__1Y(n7432_1__3__1y),
    ._4__2A(n7432_1__3__1y), ._5__2B(Rounded_exponent[2]), ._6__2Y(n7432_1__6__2y), ._7__GND(1'b0),
    ._14__Vcc(1'b1), ._13__4B(n7432_1__6__2y), ._12__4A(Rounded_exponent[3]), ._11__4Y(n7432_1__11__4y),
    ._10__3B(n7432_1__11__4y), ._9__3A(Rounded_exponent[4]), ._8__3Y(n7432_1__8__3y));
  _7432 u_7432_2 (
    ._1__1A(n7432_1__8__3y), ._2__1B(Rounded_exponent[5]), ._3__1Y(n7432_2__3__1y), ._4__2A(n7432_2__3__1y),
    ._5__2B(Rounded_exponent[6]), ._6__2Y(n7432_2__6__2y), ._7__GND(1'b0), ._14__Vcc(1'b1),
    ._13__4B(n7432_2__6__2y), ._12__4A(Rounded_exponent[7]), ._11__4Y(n7432_2__11__4y),
    ._10__3B(n7432_2__11__4y), ._9__3A(Rounded_exponent[8]), ._8__3Y(n7432_2__8__3y));
  _7432 u_7432_3 (
    ._1__1A(n7432_2__8__3y), ._2__1B(Rounded_exponent[9]), ._3__1Y(n7432_3__3__1y), ._4__2A(n7432_3__3__1y),
    ._5__2B(Rounded_exponent[10]), ._6__2Y(n7432_3__6__2y), ._7__GND(1'b0), ._14__Vcc(1'b1),
    ._13__4B(n7432_3__6__2y), ._12__4A(Rounded_exponent[11]), ._11__4Y(n7432_3__11__4y),
    ._10__3B(n7404_1__2__1y), ._9__3A(LS_Norm_borrow), ._8__3Y(Underflow));
  _7404 u_7404_1 (
    ._1__1A(n7432_3__11__4y), ._2__1Y(n7404_1__2__1y), ._14__Vcc(1'b1));  // open: _3__2A, _4__2Y, _5__3A, _6__3Y, _7__GND, _13__6A, _12__6Y, _11__5A, _10__5Y, _9__4A, _8__4Y
endmodule

// FlagUnit
module main (
  input  [11:0] Rounded_exponent,
  input  Add_sub,
  input  LS_Norm_borrow,
  input  MantissaZero,
  input  [11:0] ExpDiff,
  output Overflow,
  output Underflow,
  output Zero
);

  overflow overflow_1 (.Rounded_exponent(Rounded_exponent), .Add_sub(Add_sub), .FinalOverflow(Overflow));
  underflow underflow_1 (
    .Rounded_exponent(Rounded_exponent), .LS_Norm_borrow(LS_Norm_borrow), .Add_sub(Add_sub),
    .FinalUnderflow(Underflow));
  Zero zero_1 (.Add_sub(Add_sub), .MantissaZero(MantissaZero), .ExpDiff(ExpDiff), .Zero(Zero));

  // Notes on the sheet:
  //   Output : Overflow and Underflow flag
  //   Input : Rounded exponent from rounding unit and LS Norm borrow from subtract_circuit
endmodule

// ZeroFlag
module Zero (
  input  Add_sub,
  input  MantissaZero,
  input  [11:0] ExpDiff,
  output Zero
);

  wire bitfinder_1_found, n7408_1__3__1y, not_1_out;

  BitFinder #(.width(12)) bitfinder_1 (.in(ExpDiff), .found(bitfinder_1_found));  // open: index
  not not_1 (not_1_out, bitfinder_1_found);
  _7408 u_7408_1 (
    ._1__1A(Add_sub), ._2__1B(MantissaZero), ._3__1Y(n7408_1__3__1y), ._4__2A(n7408_1__3__1y),
    ._5__2B(not_1_out), ._6__2Y(Zero));  // open: _7__GND, _14__Vcc, _13__4B, _12__4A, _11__4Y, _10__3B, _9__3A, _8__3Y
endmodule
