// Logisim project FloatingPointAdder.circ as structural Verilog: 1 circuit, main circuit main
module main (
  input  [31:0] A,
  input  [31:0] B,
  output [31:0] out_3,
  output Overflow,
  output Underflow,
  output Zero
);

  wire Add_sub, All_zeros, C_out, Enable2sComplement, Exp_a_Exp_b, LargerExpSign, LS_Norm_borrow, RS_LS,
       RS_Norm_carry, SmallerExpSign;
  wire [11:0] Exp_diff, LS_Norm_exponent, NormalizedExponent, RS_Norm_exponent, Tentative_exp;
  wire [11:11] RoundedExponent;
  wire [19:0] LargerExpMantissa, SmallerExpMantissa;
  wire [31:0] Adder_output, LS_Norm_mantissa, NormalizedMantissa, RS_Norm_mantissa, UnsignedMantissaSum;

  RS_Norm rs_norm_1 (
    .Exponent(Tentative_exp), .Mantissa(UnsignedMantissaSum), .RS_Norm_carry(RS_Norm_carry),
    .RS_Norm_exponent(RS_Norm_exponent), .RS_Norm_mantissa(RS_Norm_mantissa));
  Multiplexer #(.width(12)) multiplexer_1 (
    .in0(LS_Norm_exponent), .in1(RS_Norm_exponent), .out(NormalizedExponent), .sel(RS_LS), .en(1'b1));
  ExponentProcessor_main main_1 (
    .ExponentA({1'b0, A[30:20]}), .ExponentB({1'b0, B[30:20]}), .Ea_Eb(Exp_a_Exp_b), .ExpDiff(Exp_diff),
    .TentativeExponent(Tentative_exp));
  MantissaPreprocessor mantissapreprocessor_1 (
    .Ea_Eb(Exp_a_Exp_b), .SmallerExpMantissa(SmallerExpMantissa), .LargerExpMantissa(LargerExpMantissa),
    .A(A), .B(B), .SmallerExpSign(SmallerExpSign), .LargerExpSign(LargerExpSign));
  MantissaCentralProcessor mantissacentralprocessor_1 (
    .ExpDiff(Exp_diff), .LargerExpSign(LargerExpSign), .SmallerExpSign(SmallerExpSign),
    .SmallerExpMantissa(SmallerExpMantissa), .LargerExpMantissa(LargerExpMantissa), .Sign_Y(out_3[31]),
    .C_out(C_out), .Enable2sComplement(Enable2sComplement), .Adder_output(Adder_output), .add_sub(Add_sub));
  MantissaPostProcessor mantissapostprocessor_1 (
    .Enable2sComplement(Enable2sComplement), .NormalizerInput(UnsignedMantissaSum), .AdderOutput(Adder_output));
  RoundingUnit roundingunit_1 (
    .AdjustedExponent({RoundedExponent[11], out_3[30:20]}), .RoundedMantissa(out_3[19:0]),
    .RoundingMantissa(NormalizedMantissa), .RoundingExponent(NormalizedExponent));
  FlagUnit_main main_2 (
    .Rounded_exponent({RoundedExponent[11], out_3[30:20]}), .Add_sub(Add_sub),
    .LS_Norm_borrow(LS_Norm_borrow), .MantissaZero(All_zeros), .ExpDiff(Exp_diff), .Overflow(Overflow),
    .Underflow(Underflow), .Zero(Zero));
  subtract_circuit_main main_3 (
    .Exponent_Input(Tentative_exp), .Input(UnsignedMantissaSum), .LS_Norm_exponent(LS_Norm_exponent),
    .LS_Norm_borrow(LS_Norm_borrow), .LS_Norm_mantissa(LS_Norm_mantissa), .All_Zeros(All_zeros));  // open: Shift_Amount
  Multiplexer #(.width(32)) multiplexer_2 (
    .in0(LS_Norm_mantissa), .in1(RS_Norm_mantissa), .out(NormalizedMantissa), .sel(RS_LS), .en(1'b1));
  Multiplexer multiplexer_3 (.in0(C_out), .in1(1'b0), .out(RS_LS), .sel(Add_sub), .en(1'b1));

  // Other names for the same wires on the sheet: Exponent_A[10:0] = A[30:20]; Mantissa_A[19:0] = A[19:0];
  //   Sign_A = A[31]; Mantissa_B[19:0] = B[19:0]; Exponent_B[10:0] = B[30:20]; Sign_B = B[31];
  //   RoundedMantissa[19:0] = out_3[19:0]; RoundedExponent[10:0] = out_3[30:20]; Sign_Y = out_3[31]
endmodule
