// Logisim project LS Norm.circ as structural Verilog: 1 circuit, main circuit LS Norm
module LS_Norm (
  input  [10:0] Exponent,
  input  [31:0] Mantissa,
  output Undeflow,
  output [10:0] Norm_exponent,
  output [31:0] Norm_mantissa
);

  wire [5:0] n32_5_priority_encoder_1_shifted_amount;
  wire [10:0] bit_extender_1_out;
  wire [31:0] shifter_1_out;

  _32_5_priority_encoder u_32_5_priority_encoder_1 (
    .Mantissa(Mantissa), .Shifted_amount(n32_5_priority_encoder_1_shifted_amount));
  assign bit_extender_1_out = {{5{1'b0}}, n32_5_priority_encoder_1_shifted_amount};  // Bit_Extender bit_extender_1
  Shifter #(.width(32)) shifter_1 (
    .in(Mantissa), .\dist (n32_5_priority_encoder_1_shifted_amount[4:0]), .out(shifter_1_out));
  Subtractor #(.width(11)) subtractor_1 (
    .a(Exponent), .b(bit_extender_1_out), .out(Norm_exponent), .bout(Undeflow));  // open: bin
  Multiplexer #(.width(32), .enable("false")) multiplexer_1 (
    .in0(shifter_1_out), .in1({32{1'b0}}), .out(Norm_mantissa),
    .sel(n32_5_priority_encoder_1_shifted_amount[5]));
endmodule
