// Logisim project Normalizer.circ as structural Verilog: 1 circuit, main circuit main
module main (
  input  [10:0] Exponent,
  input  [31:0] Mantissa,
  input  [1:0] C_S,
  output [10:0] Norm_exponent,
  output [31:0] Norm_Mantissa,
  output Overflow_Undeflow
);

  wire ls_norm_1_undeflow, not_1_out, rs_norm_1_p3;
  wire [2:0] nor_1_out;
  wire [10:0] ls_norm_1_norm_exponent, rs_norm_1_p4;
  wire [31:0] ls_norm_1_norm_mantissa, rs_norm_1_p5;

  nor nor_1 (nor_1_out[0], C_S[0], C_S[1]);
  not not_1 (not_1_out, C_S[1]);
  and and_1 (nor_1_out[2], not_1_out, C_S[0]);
  LS_Norm ls_norm_1 (
    .Exponent(Exponent), .Mantissa(Mantissa), .Undeflow(ls_norm_1_undeflow),
    .Norm_exponent(ls_norm_1_norm_exponent), .Norm_mantissa(ls_norm_1_norm_mantissa));
  // RS_Norm rs_norm_1: pin names not known; wires that end beside it: Exponent, Mantissa, rs_norm_1_p3, rs_norm_1_p4, rs_norm_1_p5
  Multiplexer #(.select(3), .width(11), .enable("false")) multiplexer_1 (
    .in1(ls_norm_1_norm_exponent), .in2(rs_norm_1_p4), .in4(Exponent), .out(Norm_exponent),
    .sel({nor_1_out[2], C_S[1], nor_1_out[0]}));  // open: in0, in3, in5, in6, in7
  Multiplexer #(.select(3), .width(32), .enable("false")) multiplexer_2 (
    .in1(ls_norm_1_norm_mantissa), .in2(rs_norm_1_p5), .in4(Mantissa), .out(Norm_Mantissa),
    .sel({nor_1_out[2], C_S[1], nor_1_out[0]}));  // open: in0, in3, in5, in6, in7
  Multiplexer #(.select(3), .enable("false")) multiplexer_3 (
    .in1(ls_norm_1_undeflow), .in2(rs_norm_1_p3), .in3(1'b0), .out(Overflow_Undeflow),
    .sel({nor_1_out[2], C_S[1], nor_1_out[0]}));  // open: in0, in4, in5, in6, in7
endmodule
