// Logisim project RS Norm.circ as structural Verilog: 1 circuit, main circuit RS Norm
// RS normalizer
module RS_Norm (
  input  [11:0] Exponent,
  input  [31:0] Mantissa,
  output RS_Norm_carry,
  output [11:0] RS_Norm_exponent,
  output [31:0] RS_Norm_mantissa
);

  wire [31:31] shifter_1_out;

  Adder #(.width(12)) adder_1 (.a(Exponent), .b(12'h1), .out(RS_Norm_exponent), .cout(RS_Norm_carry));  // open: cin
  Shifter #(.width(32), .shift("lr")) shifter_1 (
    .in(Mantissa), .\dist (5'b00001), .out({shifter_1_out[31], RS_Norm_mantissa[30:0]}));

  assign RS_Norm_mantissa[31] = 1'b1;
endmodule
