// Logisim project priorioty-encoder.circ as structural Verilog: 1 circuit, main circuit 32*5_priority_encoder
module _32_5_priority_encoder (
  input  [31:0] Mantissa,
  output [5:0] Shifted_amount
);

  wire priority_encoder_1_gs;
  wire [4:0] multiplexer_1_out, not_1_out, priority_encoder_1_out;

  Priority_Encoder #(.select(5)) priority_encoder_1 (
    .in0(Mantissa[0]), .in1(Mantissa[1]), .in2(Mantissa[2]), .in3(Mantissa[3]), .in4(Mantissa[4]),
    .in5(Mantissa[5]), .in6(Mantissa[6]), .in7(Mantissa[7]), .in8(Mantissa[8]), .in9(Mantissa[9]),
    .in10(Mantissa[10]), .in11(Mantissa[11]), .in12(Mantissa[12]), .in13(Mantissa[13]), .in14(Mantissa[14]),
    .in15(Mantissa[15]), .in16(Mantissa[16]), .in17(Mantissa[17]), .in18(Mantissa[18]), .in19(Mantissa[19]),
    .in20(Mantissa[20]), .in21(Mantissa[21]), .in22(Mantissa[22]), .in23(Mantissa[23]), .in24(Mantissa[24]),
    .in25(Mantissa[25]), .in26(Mantissa[26]), .in27(Mantissa[27]), .in28(Mantissa[28]), .in29(Mantissa[29]),
    .in30(Mantissa[30]), .in31(Mantissa[31]), .out(priority_encoder_1_out), .gs(priority_encoder_1_gs));  // open: en_out, en_in
  Multiplexer #(.width(5), .disabled(0), .enable("false")) multiplexer_1 (
    .in0({5{1'b0}}), .in1(priority_encoder_1_out), .out(multiplexer_1_out), .sel(priority_encoder_1_gs));
  assign not_1_out = ~multiplexer_1_out;  // NOT_Gate not_1, 5 bits wide
  Adder #(.width(5)) adder_1 (
    .a(not_1_out), .b({5{1'b0}}), .out(Shifted_amount[4:0]), .cin(1'b1), .cout(Shifted_amount[5]));
endmodule
