// Logisim project MIPS.circ as structural Verilog: 2 circuits, main circuit main
module main (
  input  reset,
  output [3:0] ReadData1,
  output [3:0] ReadData2,
  output [3:0] t0,
  output [3:0] t1,
  output [3:0] t2,
  output [3:0] t3,
  output [3:0] t4,
  output [3:0] sp
);

  wire and_1_out, and_2_out, Clk_out, control_unit_1_alusrc, control_unit_1_bneq, control_unit_1_branch,
       control_unit_1_jump, control_unit_1_memread, control_unit_1_memtoreg, control_unit_1_memwrite,
       control_unit_1_regdst, control_unit_1_regwrite, main_3_zero_flag, not_1_out, or_1_out;
  wire [2:0] control_unit_1_aluop;
  wire [3:0] datamemory_1_datatowrite, main_1_dst_reg, main_1_instruction__7_4, main_1_instruction__11_8,
       main_1_opcode, main_3_out_4, multiplexer_1_out;
  wire [7:0] adder_1_out, adder_2_out, main_1_instruction__3_0, main_1_instruction__11_4, main_1_pc,
       multiplexer_2_out, multiplexer_3_out;

  Clock Clk (.out(Clk_out));
  // Probe on multiplexer_2_out
  instruction_memory_main main_1 (
    .PC_Input(multiplexer_2_out),
    .Instruction__3_0({main_1_instruction__3_0[7], main_1_instruction__3_0[2:0]}), .Dst_Reg(main_1_dst_reg),
    .RegDst(control_unit_1_regdst), .Instruction__7_4(main_1_instruction__7_4),
    .Instruction__11_8(main_1_instruction__11_8), .Opcode(main_1_opcode),
    .Instruction__11_4(main_1_instruction__11_4), .Clock(Clk_out), .PC(main_1_pc), .Reset(reset));
  Adder adder_1 (.a(8'h1), .b(main_1_pc), .out(adder_1_out), .cin(1'b0));  // open: cout
  Control_Unit control_unit_1 (
    .Opcode(main_1_opcode), .ALUOp(control_unit_1_aluop), .Branch(control_unit_1_branch),
    .Jump(control_unit_1_jump), .Bneq(control_unit_1_bneq), .MemtoReg(control_unit_1_memtoreg),
    .MemRead(control_unit_1_memread), .MemWrite(control_unit_1_memwrite), .RegWrite(control_unit_1_regwrite),
    .RegDst(control_unit_1_regdst), .ALUSrc(control_unit_1_alusrc));
  Adder adder_2 (
    .a(adder_1_out), .b({{5{main_1_instruction__3_0[7]}}, main_1_instruction__3_0[2:0]}), .out(adder_2_out),
    .cin(1'b0));  // open: cout
  RegisterFile4_main main_2 (
    .ReadReg1(main_1_instruction__11_8), .ReadReg2(main_1_instruction__7_4),
    .WriteData(datamemory_1_datatowrite), .WriteReg(main_1_dst_reg),
    .RegWriteEnable(control_unit_1_regwrite), .Clock(Clk_out), .RegData1(ReadData1), .RegData2(ReadData2),
    .t0(t0), .t1(t1), .t2(t2), .t3(t3), .t4(t4), .sp(sp));  // open: t5
  Multiplexer #(.width(4)) multiplexer_1 (
    .in0(ReadData2), .in1({main_1_instruction__3_0[7], main_1_instruction__3_0[2:0]}),
    .out(multiplexer_1_out), .sel(control_unit_1_alusrc), .en(1'b1));
  not not_1 (not_1_out, main_3_zero_flag);
  Alu_main main_3 (
    .A(ReadData1), .B(multiplexer_1_out), .S(control_unit_1_aluop), .out_4(main_3_out_4),
    .Zero_Flag(main_3_zero_flag));
  and and_1 (and_1_out, control_unit_1_bneq, not_1_out);
  and and_2 (and_2_out, control_unit_1_branch, main_3_zero_flag);
  DataMemory datamemory_1 (
    .ALUOutput(main_3_out_4), .RegData(ReadData2), .MemWrite(control_unit_1_memwrite), .Clock(Clk_out),
    .MemRead(control_unit_1_memread), .MemToReg(control_unit_1_memtoreg),
    .DataToWrite(datamemory_1_datatowrite));
  Multiplexer #(.width(8)) multiplexer_2 (
    .in0(multiplexer_3_out), .in1(main_1_instruction__11_4), .out(multiplexer_2_out),
    .sel(control_unit_1_jump), .en(1'b1));
  or or_1 (or_1_out, and_1_out, and_2_out);
  Multiplexer #(.width(8)) multiplexer_3 (
    .in0(adder_1_out), .in1(adder_2_out), .out(multiplexer_3_out), .sel(or_1_out), .en(1'b1));
endmodule

module test (
  input  [7:0] in_1,
  output [15:0] out_2
);

  ROM #(.dataWidth(16)) rom_1 (.addr(in_1), .data(out_2));  // open: sel

  // Notes on the sheet:
  //   contents of rom_1 (hex, n*v repeats v):
  //   1254 1112 1234 5678 7895
endmodule
