// Logisim project instruction_memory.circ as structural Verilog: 2 circuits, main circuit main
module main (
  input  [7:0] PC_Input,
  input  RegDst,
  input  Clock,
  input  Reset,
  output [3:0] Instruction__3_0,
  output [7:0] PC,
  output [3:0] Dst_Reg,
  output [3:0] Instruction__7_4,
  output [3:0] Instruction__11_8,
  output [3:0] Opcode,
  output [7:0] Instruction__11_4
);

  Register register_1 (.D(PC_Input), .en(1'b1), .Q(PC), .clk(Clock), .clr(Reset));
  ROM #(.dataWidth(16)) rom_1 (
    .addr(PC), .data({Opcode, Instruction__11_4[7:4], Instruction__7_4, Instruction__3_0}), .sel(1'b1));
  Multiplexer #(.width(4)) multiplexer_1 (
    .in0(Instruction__7_4), .in1(Instruction__3_0), .out(Dst_Reg), .sel(RegDst), .en(1'b1));

  assign Instruction__11_4[3:0] = Instruction__7_4;
  assign Instruction__11_8 = Instruction__11_4[7:4];

  // Notes on the sheet:
  //   contents of rom_1 (hex, n*v repeats v):
  //   a000 7000 5000 6000 0 1000 9000 b000 8000 d000 e000 f000 c000 2000 4000 3000
endmodule

module test (
);

  main main_1 ();  // open: PC_Input, Instruction__3_0, Dst_Reg, RegDst, Instruction__7_4, Instruction__11_8, Opcode, Instruction__11_4, Clock, PC, Reset
endmodule
